// Logisim project TallerLogica-Combinatorios-individual.circ as structural Verilog: 14 circuits, main circuit verificador
module sumador_simple (
  input  A,
  input  B,
  output S,
  output Cout
);

  xor xor_1 (S, A, B);
  and and_1 (Cout, A, B);
endmodule

module sumador_completo (
  input  A,
  input  B,
  input  Cin,
  output S,
  output Cout
);

  wire sumador_simple_1_cout, sumador_simple_1_s, sumador_simple_2_cout;

  sumador_simple sumador_simple_1 (.A(A), .B(B), .S(sumador_simple_1_s), .Cout(sumador_simple_1_cout));
  sumador_simple sumador_simple_2 (.A(sumador_simple_1_s), .B(Cin), .S(S), .Cout(sumador_simple_2_cout));
  or or_1 (Cout, sumador_simple_2_cout, sumador_simple_1_cout);
endmodule

module sumador_4 (
  input  Cin,
  input  [3:0] A,
  input  [3:0] B,
  output [3:0] S,
  output Cout
);

  wire sumador_completo_1_cout, sumador_completo_2_cout, sumador_completo_3_cout;

  Hex_Digit_Display hex_digit_display_1 (.value(A));  // open: dp
  Hex_Digit_Display hex_digit_display_2 (.value(B));  // open: dp
  sumador_completo sumador_completo_1 (.A(A[0]), .B(B[0]), .Cin(Cin), .S(S[0]), .Cout(sumador_completo_1_cout));
  sumador_completo sumador_completo_2 (
    .A(A[1]), .B(B[1]), .Cin(sumador_completo_1_cout), .S(S[1]), .Cout(sumador_completo_2_cout));
  sumador_completo sumador_completo_3 (
    .A(A[2]), .B(B[2]), .Cin(sumador_completo_2_cout), .S(S[2]), .Cout(sumador_completo_3_cout));
  sumador_completo sumador_completo_4 (.A(A[3]), .B(B[3]), .Cin(sumador_completo_3_cout), .S(S[3]), .Cout(Cout));
  Hex_Digit_Display hex_digit_display_3 (.value(S));  // open: dp
endmodule

module comparador_cero (
  input  [3:0] A,
  output Z
);

  wire not_1_out, not_2_out, not_3_out, not_4_out;

  Hex_Digit_Display hex_digit_display_1 (.value(A));  // open: dp
  not not_1 (not_1_out, A[0]);
  not not_2 (not_2_out, A[1]);
  not not_3 (not_3_out, A[2]);
  not not_4 (not_4_out, A[3]);
  and and_1 (Z, not_1_out, not_2_out, not_3_out, not_4_out);
endmodule

module sumador_flags (
  input  Cin,
  input  [3:0] A,
  input  [3:0] B,
  output [3:0] S,
  output C,
  output N,
  output Z,
  output V
);

  sumador_4 sumador_4_1 (.Cin(Cin), .A(A), .B(B), .S({N, S[2:0]}), .Cout(C));
  comparador_cero comparador_cero_1 (.A({N, S[2:0]}), .Z(Z));
  comp_overflow comp_overflow_1 (.c3(N), .a3(A[3]), .b3(B[3]), .O(V));

  assign S[3] = N;
endmodule

module incrementador_4 (
  input  [3:0] A,
  output [3:0] S
);

  sumador_4 sumador_4_1 (.A(A), .B(4'b0001), .S(S));  // open: Cin, Cout
  Hex_Digit_Display hex_digit_display_1 (.value(S));  // open: dp
endmodule

module inversor_4 (
  input  [3:0] A,
  input  INV,
  output [3:0] S
);

  wire [3:0] incrementador_4_1_s, not_1_out;

  not not_1 (not_1_out[0], A[0]);
  not not_2 (not_1_out[1], A[1]);
  not not_3 (not_1_out[2], A[2]);
  not not_4 (not_1_out[3], A[3]);
  Multiplexer #(.width(4)) multiplexer_1 (.in0(A), .in1(incrementador_4_1_s), .out(S), .sel(INV));
  incrementador_4 incrementador_4_1 (.A(not_1_out), .S(incrementador_4_1_s));
  Hex_Digit_Display hex_digit_display_1 (.value(S));  // open: dp
endmodule

module ALU (
  input  [3:0] A,
  input  [3:0] B,
  input  [1:0] OP,
  output N,
  output Z,
  output V,
  output C,
  output [3:0] S
);

  wire comparador_cero_1_z, sC, sN, sV, sZ;
  wire [3:0] inversor_4_1_s, sAND, sOR, sS;

  inversor_4 inversor_4_1 (.A(B), .INV(OP[0]), .S(inversor_4_1_s));
  assign sAND = A & B;  // AND_Gate and_1, 4 bits wide
  assign sOR = A | B;  // OR_Gate or_1, 4 bits wide
  sumador_flags sumador_flags_1 (.Cin(1'b0), .A(A), .B(inversor_4_1_s), .S(sS), .C(sC), .N(sN), .Z(sZ), .V(sV));
  comparador_cero comparador_cero_1 (.A(S), .Z(comparador_cero_1_z));
  circ_overflow circ_overflow_1 (.in_1(sV), .B(B), .in_3(OP), .V(V));
  circ_carry circ_carry_1 (.in_1(sC), .B(B), .in_3(OP), .C(C));
  Multiplexer #(.select(2), .width(4)) multiplexer_1 (.in0(sS), .in1(sS), .in2(sAND), .in3(sOR), .out(S), .sel(OP));
  Multiplexer #(.select(2)) multiplexer_2 (.in0(sN), .in1(sN), .in2(S[3]), .in3(S[3]), .out(N), .sel(OP));
  Multiplexer #(.select(2)) multiplexer_3 (
    .in0(sZ), .in1(sZ), .in2(comparador_cero_1_z), .in3(comparador_cero_1_z), .out(Z), .sel(OP));
endmodule

module verificador (
  output [3:0] out_1,
  output [3:0] out_2,
  output [1:0] out_3,
  output halt,
  output N,
  output Z,
  output V,
  output C,
  output [3:0] res
);

  wire clock_1_out;

  Clock clock_1 (.out(clock_1_out));
  Counter #(.max('h3ff), .width(10)) counter_1 (
    .clk(clock_1_out), .carry(halt), .Q({out_3, out_2, out_1}));  // open: clr, load, up, count, D
  ALU alu_1 (.A(out_1), .B(out_2), .OP(out_3), .N(N), .Z(Z), .V(V), .C(C), .S(res));
endmodule

module overflow_resta (
  input  V_in,
  input  [3:0] B,
  output V_out
);

  wire comparador_cero_1_z, not_2_out;
  wire [3:3] not_1_out;

  not not_1 (not_1_out[3], B[3]);
  not not_2 (not_2_out, V_in);
  comparador_cero comparador_cero_1 (.A({not_1_out[3], B[2:0]}), .Z(comparador_cero_1_z));
  Multiplexer multiplexer_1 (.in0(V_in), .in1(not_2_out), .out(V_out), .sel(comparador_cero_1_z));
endmodule

module comp_overflow (
  input  c3,
  input  a3,
  input  b3,
  output O
);

  wire not_1_out, xor_1_out, xor_2_out;

  xor xor_1 (xor_1_out, c3, a3);
  not not_1 (not_1_out, xor_2_out);
  xor xor_2 (xor_2_out, a3, b3);
  and and_1 (O, xor_1_out, not_1_out);
endmodule

module comp_carry (
  input  in_1,
  input  [3:0] in_2,
  output out_3
);

  wire comparador_cero_1_z, not_1_out;

  not not_1 (not_1_out, comparador_cero_1_z);
  comparador_cero comparador_cero_1 (.A(in_2), .Z(comparador_cero_1_z));
  and and_1 (out_3, in_1, not_1_out);
endmodule

module circ_carry (
  input  in_1,
  input  [3:0] B,
  input  [1:0] in_3,
  output C
);

  wire comp_carry_1_out_3, not_1_out;

  not not_1 (not_1_out, in_1);
  comp_carry comp_carry_1 (.in_1(not_1_out), .in_2(B), .out_3(comp_carry_1_out_3));
  Multiplexer #(.select(2)) multiplexer_1 (
    .in0(in_1), .in1(comp_carry_1_out_3), .in2(1'b0), .in3(1'b0), .out(C), .sel(in_3));
endmodule

module circ_overflow (
  input  in_1,
  input  [3:0] B,
  input  [1:0] in_3,
  output V
);

  wire overflow_resta_1_v_out;

  overflow_resta overflow_resta_1 (.V_in(in_1), .B(B), .V_out(overflow_resta_1_v_out));
  Multiplexer #(.select(2)) multiplexer_1 (
    .in0(in_1), .in1(overflow_resta_1_v_out), .in2(1'b0), .in3(1'b0), .out(V), .sel(in_3));
endmodule
